# Fritzing sketch MZ_7SegDiceWithSound (saved by Fritzing 0.9.4)
breadboards: 1

parts:
  Part1 = Arduino Uno (Rev3)
  7_Segment1 = 7 Segment Display
  R1 = Resistor [tolerance=±5% resistance=220 package=THT]
  S1 = Pushbutton [package="[THT]"]
  R2 = Resistor [tolerance=±5% resistance=220 package=THT]
  J1 = Piezo Speaker

nets:
  N1: Part1.D8, 7_Segment1.Segment_D
  N2: Part1.D9_PWM, 7_Segment1.Segment_E
  N3: Part1.D10_PWM/SS, S1.Pin_3, S1.Pin_4, R2.Pin_0
  N4: Part1.D11_PWM/MOSI, J1.pin2
  N5: Part1.D2, 7_Segment1.Segment_A#1
  N6: Part1.D3_PWM, 7_Segment1.Segment_F
  N7: Part1.D4, 7_Segment1.Segment_A#10
  N8: Part1.D5_PWM, 7_Segment1.Segment_B
  N9: Part1.D6_PWM, 7_Segment1.Segment_DP
  N10: Part1.D7, 7_Segment1.Segment_C
  N11: Part1.5V, S1.Pin_1, S1.Pin_2
  N12: Part1.GND, R1.Pin_0, R2.Pin_1, J1.pin1
  N13: 7_Segment1.common_cathode#8, R1.Pin_1
