# Fritzing sketch MZ_7SegmentStopwatch (saved by Fritzing 0.9.4)
breadboards: 1

parts:
  LED1 = 7-SEGMENT-4DIGIT-YOUNGSUN [package=7-segment-4digit-youngsun-longpads]
  R1 = Resistor [tolerance=±5% resistance=220 package=THT]
  R2 = Resistor [tolerance=±5% resistance=220 package=THT]
  R3 = Resistor [tolerance=±5% resistance=220 package=THT]
  R4 = Resistor [tolerance=±5% resistance=220 package=THT]
  R5 = Resistor [tolerance=±5% resistance=220 package=THT]
  R6 = Resistor [tolerance=±5% resistance=220 package=THT]
  R7 = Resistor [tolerance=±5% resistance=220 package=THT]
  R8 = Resistor [tolerance=±5% resistance=220 package=THT]
  Start/Stop = Momentary Switch [package=tactile-pth]
  Part1 = Arduino Uno (Rev3)
  R9 = Resistor [tolerance=±5% resistance=10k package=THT]
  Reset = Momentary Switch [package=tactile-pth]

nets:
  N1: LED1.COL-A, R5.Pin_1
  N2: LED1.E, R4.Pin_0
  N3: LED1.DIG3, R8.Pin_1
  N4: LED1.DP, R3.Pin_0
  N5: LED1.DIG4, R7.Pin_1
  N6: R1.Pin_1, Part1.D6_PWM
  N7: R2.Pin_1, Part1.D7
  N8: R3.Pin_1, Part1.D8
  N9: R4.Pin_1, Part1.D9_PWM
  N10: R5.Pin_0, Part1.D10_PWM/SS
  N11: R6.Pin_0, Part1.D11_PWM/MOSI
  N12: R7.Pin_0, Part1.D12/MISO
  N13: R8.Pin_0, Part1.D13/SCK
  N14: Start/Stop.1, R9.Pin_0
  N15: Start/Stop.3, Part1.5V, R9.Pin_1, Reset.3
  N16: Start/Stop.4, Part1.A0
  N17: Part1.A1, Reset.4
