# Fritzing sketch MZ_BikeLight (saved by Fritzing 0.9.4)
breadboards: 1

parts:
  Part1 = Arduino Uno (Rev3)
  LED1 = LED - 3mm [color="Red (633nm)" part_number=LED1 package="3 mm [THT]"]
  LED2 = LED - 3mm [color="Red (633nm)" part_number=LED2 package="3 mm [THT]"]
  LED3 = LED - 3mm [color="Red (633nm)" part_number=LED3 package="3 mm [THT]"]
  R1 = Resistor [tolerance=±5% resistance=330 package=THT]
  R2 = Resistor [tolerance=±5% resistance=330 package=THT]
  R3 = Resistor [tolerance=±5% resistance=330 package=THT]
  S1 = Pushbutton [package="[THT]"]
  R4 = Resistor [tolerance=±5% resistance=220 package=THT]

nets:
  N1: Part1.D12/MISO, S1.Pin_3, S1.Pin_4, R4.Pin_1
  N2: Part1.D2, R1.Pin_0
  N3: Part1.D3_PWM, R2.Pin_0
  N4: Part1.D4, R3.Pin_0
  N5: Part1.5V, S1.Pin_1, S1.Pin_2
  N6: Part1.GND, LED1.cathode, LED2.cathode, LED3.cathode, R4.Pin_0
  N7: LED1.anode, R1.Pin_1
  N8: LED2.anode, R2.Pin_1
  N9: LED3.anode, R3.Pin_1
