# Fritzing sketch MZ_LEDMatrix72xxDemo (saved by Fritzing 0.9.4)

parts:
  Part1 = Arduino Nano (Rev3.0)
  8x8_LED_Modul_mit_MAX1 = 8x8 LED Modul mit MAX7219 [package=THT]

nets:
  N1: Part1.D2, 8x8_LED_Modul_mit_MAX1.DIN_Eingang
  N2: Part1.D3, 8x8_LED_Modul_mit_MAX1.CS_Eingang
  N3: Part1.D4, 8x8_LED_Modul_mit_MAX1.CLK_Eingang
  N4: Part1.GND, 8x8_LED_Modul_mit_MAX1.GND_Eingang
  N5: Part1.5V, 8x8_LED_Modul_mit_MAX1.VCC_Eingang
